// Digital circuit somadoresEaprendizado.dig as structural Verilog
module somadoresEaprendizado (
  input  Cin,
  input  x3,
  input  x2,
  input  x1,
  input  x0,
  input  y3,
  input  y2,
  input  y1,
  input  y0,
  input  x6,
  input  x7,
  input  A3,
  input  B3,
  input  B2,
  input  B1,
  input  B0,
  input  A2,
  input  A1,
  input  A0,
  input  Cin_2,
  input  Cin_3,
  input  x,
  input  y,
  output r8,
  output r9,
  output r10,
  output r11,
  output Overflow,
  output Soma,
  output Cout,
  output Overflow_2
);

  wire add_2_c_o, add_3_c_o, add_4_c_o, and_1_out, and_2_out, and_3_out, and_4_out, and_5_out, and_6_out,
       and_7_out, and_8_out, and_9_out, and_10_out, not_1_out, not_2_out, or_3_out, or_4_out, or_5_out,
       xor_1_out, xor_3_out, xor_5_out, xor_7_out, xor_9_out;
  wire [3:0] add_4_s, xor_10_out;

  and and_1 (and_1_out, y, x);
  or or_1 (Cout, and_2_out, and_1_out);
  and and_2 (and_2_out, Cin_3, xor_1_out);
  xor xor_1 (xor_1_out, y, x);
  xor xor_2 (Soma, Cin_3, xor_1_out);
  and and_3 (and_3_out, y3, x3);
  and and_4 (and_4_out, or_3_out, xor_3_out);
  or or_2 (Overflow_2, and_4_out, and_3_out);
  xor xor_3 (xor_3_out, y3, x3);
  xor xor_4 (xor_10_out[3], or_3_out, xor_3_out);
  and and_5 (and_5_out, y2, x2);
  or or_3 (or_3_out, and_6_out, and_5_out);
  and and_6 (and_6_out, or_4_out, xor_5_out);
  xor xor_5 (xor_5_out, y2, x2);
  xor xor_6 (xor_10_out[2], or_4_out, xor_5_out);
  Seven_Seg_Hex seven_seg_hex_1 (.d(xor_10_out), .dp(1'b0));
  and and_7 (and_7_out, y1, x1);
  or or_4 (or_4_out, and_8_out, and_7_out);
  and and_8 (and_8_out, or_5_out, xor_7_out);
  xor xor_7 (xor_7_out, y1, x1);
  xor xor_8 (xor_10_out[1], or_5_out, xor_7_out);
  and and_9 (and_9_out, y0, x0);
  and and_10 (and_10_out, Cin, xor_9_out);
  or or_5 (or_5_out, and_10_out, and_9_out);
  xor xor_9 (xor_9_out, y0, x0);
  xor xor_10 (xor_10_out[0], Cin, xor_9_out);
  Seven_Seg_Hex seven_seg_hex_2 (.d({B3, B2, B1, B0}), .dp(1'b0));
  Add add_1 (.a(B3), .b(A3), .c_i(add_2_c_o), .s(add_4_s[3]), .c_o(Overflow));
  Seven_Seg_Hex seven_seg_hex_3 (.d(add_4_s), .dp(1'b0));
  Add add_2 (.a(B2), .b(A2), .c_i(add_3_c_o), .s(add_4_s[2]), .c_o(add_2_c_o));
  Add add_3 (.a(B1), .b(A1), .c_i(add_4_c_o), .s(add_4_s[1]), .c_o(add_3_c_o));
  Add add_4 (.a(B0), .b(A0), .c_i(Cin_2), .s(add_4_s[0]), .c_o(add_4_c_o));
  Seven_Seg_Hex seven_seg_hex_4 (.d({A3, A2, A1, A0}), .dp(1'b0));
  not not_1 (not_1_out, x7);
  and and_11 (r10, x6, not_1_out);
  and and_12 (r11, x7, x6);
  not not_2 (not_2_out, x6);
  and and_13 (r9, not_2_out, x7);
  and and_14 (r8, not_2_out, not_1_out);

  // Notes on the sheet:
  //   Somador completo sozinho
  //   Somador de 4 bits com representação de cada porta lógica
  //   somador de 4 bits completo
  //   Decoder
endmodule
